# Fritzing sketch 15. Schematics (saved by Fritzing 0.9.3b)
circuit board: 8.46667cm x 5.64444cm
breadboards: 1

parts:
  Part1 = Arduino Uno (Rev3)
  LED1 = RGB LED (com. cathode, rgb) [package="5 mm [THT]"]
  R1 = Resistor [tolerance=±5% resistance=220 package=THT]
  R2 = Resistor [tolerance=±5% resistance=220 package=THT]
  R3 = Resistor [tolerance=±5% resistance=220 package=THT]
  R4 = Rotary Potentiometer (Small) [maximum_resistance=100kΩ package=THT]
  S1 = Pushbutton [package="[THT]"]
  R5 = Resistor [tolerance=±5% resistance=10k package=THT]  # not connected

nets:
  N1: Part1.A0, R4.wiper
  N2: Part1.D9_PWM, R1.Pin_1
  N3: Part1.D10_PWM/SS, R2.Pin_1
  N4: Part1.D11_PWM/MOSI, R3.Pin_1
  N5: Part1.GND, LED1.common_cathode
  N6: Part1.D2, S1.Pin_1, S1.Pin_2
  N7: Part1.5V, R4.leg1, R4.leg2, S1.Pin_3, S1.Pin_4
  N8: LED1.red_anode, R1.Pin_0
  N9: LED1.green_anode, R2.Pin_0
  N10: LED1.blue_anode, R3.Pin_0
